// Logisim project sagui.circ as structural Verilog
module main (
);

  wire clk, cls;
  wire [23:0] adder_1_out, register_1_q;

  Adder #(.width(24)) adder_1 (.a(register_1_q), .b(24'h1), .out(adder_1_out), .cin(1'b0));  // open: cout
  Register #(.width(24)) register_1 (.D(adder_1_out), .en(1'b1), .clk(clk), .Q(register_1_q), .clr(cls));
  Clock clock_1 (.out(clk));
  ROM #(.addrWidth(24)) rom_1 (.addr(register_1_q));  // open: data
  Button button_1 (.out(cls));
  MemControle memcontrole_1 ();  // open: Entrada
endmodule

module MemControle (
  input  [3:0] Entrada
);

  ROM #(.addrWidth(4)) rom_1 (.addr(Entrada));  // open: data
endmodule

module bancoRegs (
  input  [7:0] dadosEscrita,
  input  write,
  input  clk,
  input  rst,
  input  [1:0] ra,
  input  [1:0] rb,
  output [7:0] saidaA,
  output [7:0] saidaB
);

  wire [7:0] demultiplexer_1_out0, demultiplexer_1_out1, demultiplexer_1_out2, demultiplexer_1_out3,
       register_1_q, register_2_q, register_3_q;

  Register register_1 (.D(demultiplexer_1_out1), .en(write), .clk(clk), .Q(register_1_q), .clr(rst));
  Multiplexer #(.select(2), .width(8)) multiplexer_1 (
    .in0({8{1'b0}}), .in1(register_1_q), .in2(register_2_q), .in3(register_3_q), .out(saidaA), .sel(ra));
  Multiplexer #(.select(2), .width(8)) multiplexer_2 (
    .in0({8{1'b0}}), .in1(register_1_q), .in2(register_2_q), .in3(register_3_q), .out(saidaB), .sel(rb));
  Demultiplexer #(.select(2), .width(8)) demultiplexer_1 (
    .out0(demultiplexer_1_out0), .out1(demultiplexer_1_out1), .out2(demultiplexer_1_out2),
    .out3(demultiplexer_1_out3), .in(dadosEscrita), .sel(ra));
  Register register_2 (.D(demultiplexer_1_out2), .en(write), .clk(clk), .Q(register_2_q), .clr(rst));
  Register register_3 (.D(demultiplexer_1_out3), .en(write), .clk(clk), .Q(register_3_q), .clr(rst));
  // also tied to GND on the sheet: {demultiplexer_1_out0[0], demultiplexer_1_out0[1], demultiplexer_1_out0[2], demultiplexer_1_out0[3], demultiplexer_1_out0[4], demultiplexer_1_out0[5], demultiplexer_1_out0[6], demultiplexer_1_out0[7]}
endmodule
